// Logisim project partial-store.circ as structural Verilog: 1 circuit, main circuit partial_store
module partial_store (
  input  [31:0] Instruction,
  input  [31:0] MemAddress,
  input  [31:0] DataFromReg,
  input  MemWEn,
  output [3:0] MemWriteMask,
  output [31:0] DataToMem
);

  wire [3:0] multiplexer_4_out, sb_MemWriteMask, sh_MemWriteMask;
  wire [31:0] sb_DataFromReg, sh_DataFromReg;

  Multiplexer #(.select(2), .width(4)) multiplexer_1 (
    .in0(4'b0001), .in1(4'b0010), .in2(4'b0100), .in3(4'b1000), .out(sb_MemWriteMask), .sel(MemAddress[1:0]));
  Multiplexer #(.width(4)) multiplexer_2 (.in0(4'b0011), .in1(4'b1100), .out(sh_MemWriteMask), .sel(MemAddress[1]));
  Multiplexer #(.select(2), .width(32)) multiplexer_3 (
    .in0({{24{1'b0}}, DataFromReg[7:0]}), .in1({{16{1'b0}}, DataFromReg[7:0], {8{1'b0}}}),
    .in2({{8{1'b0}}, DataFromReg[7:0], {16{1'b0}}}), .in3({DataFromReg[7:0], {24{1'b0}}}),
    .out(sb_DataFromReg), .sel(MemAddress[1:0]));
  Multiplexer #(.select(3), .width(4)) multiplexer_4 (
    .in0(sb_MemWriteMask), .in1(sh_MemWriteMask), .in2(4'b1111), .out(multiplexer_4_out),
    .sel(Instruction[14:12]));  // open: in3, in4, in5, in6, in7
  Multiplexer #(.width(4)) multiplexer_5 (.in0(4'b0000), .in1(multiplexer_4_out), .out(MemWriteMask), .sel(MemWEn));
  Multiplexer #(.width(32)) multiplexer_6 (
    .in0({{16{1'b0}}, DataFromReg[15:0]}), .in1({DataFromReg[15:0], {16{1'b0}}}), .out(sh_DataFromReg),
    .sel(MemAddress[1]));
  Multiplexer #(.select(3), .width(32)) multiplexer_7 (
    .in0(sb_DataFromReg), .in1(sh_DataFromReg), .in2(DataFromReg), .out(DataToMem), .sel(Instruction[14:12]));  // open: in3, in4, in5, in6, in7

  // Other names for the same wires on the sheet: Bottom_8_bits[7:0] = DataFromReg[7:0];
  //   Bottom_16_bits[15:0] = DataFromReg[15:0]; opcode[6:0] = Instruction[6:0]; rd[4:0] = Instruction[11:7];
  //   func3[2:0] = Instruction[14:12]; rs1[4:0] = Instruction[19:15]; rs2[4:0] = Instruction[24:20];
  //   func7[6:0] = Instruction[31:25]

  // Notes on the sheet:
  //   INPUTS to your circuit
  //   1000
  //   0100
  //   address最后两位
  //   0010
  //   DON'T CHANGE THE LOCATIONS OF THE INPUTS AND OUTPUTS!
  //   0001
  //   OUTPUT from your circuit
  //   address倒数第二位
  //   1100
  //   0011
  //   Docode
  //   1111
  //   控制内存是否可写
endmodule
