// Logisim project regfile.circ as structural Verilog: 1 circuit, main circuit regfile
module regfile (
  input  [4:0] ReadIndex1,
  input  [4:0] ReadIndex2,
  input  [4:0] WriteIndex,
  input  [31:0] WriteData,
  input  RegWEn,
  input  clk,
  output [31:0] ra,
  output [31:0] sp,
  output [31:0] t0,
  output [31:0] t1,
  output [31:0] t2,
  output [31:0] s0,
  output [31:0] s1,
  output [31:0] a0,
  output [31:0] ReadData1,
  output [31:0] ReadData2
);

  wire En0, En1, En2, En3, En4, En5, En6, En7, En8, En9, En10, En11, En12, En13, En14, En15, En16, En17,
       En18, En19, En20, En21, En22, En23, En24, En25, En26, En27, En28, En29, En30, En31;
  wire [31:0] a1, a2, a3, a4, a5, a6, a7, gp, s2, s3, s4, s5, s6, s7, s8, s9, s10, s11, t3, t4, t5, t6, tp,
       zero;

  Demultiplexer #(.select(5)) demultiplexer_1 (
    .out0(En0), .out1(En1), .out2(En2), .out3(En3), .out4(En4), .out5(En5), .out6(En6), .out7(En7),
    .out8(En8), .out9(En9), .out10(En10), .out11(En11), .out12(En12), .out13(En13), .out14(En14),
    .out15(En15), .out16(En16), .out17(En17), .out18(En18), .out19(En19), .out20(En20), .out21(En21),
    .out22(En22), .out23(En23), .out24(En24), .out25(En25), .out26(En26), .out27(En27), .out28(En28),
    .out29(En29), .out30(En30), .out31(En31), .in(RegWEn), .sel(WriteIndex));
  Register #(.width(32)) register_1 (.D({32{1'b0}}), .en(En0), .clk(clk), .Q(zero));  // open: clr
  Register #(.width(32)) register_2 (.D(WriteData), .en(En1), .clk(clk), .Q(ra));  // open: clr
  Register #(.width(32)) register_3 (.D(WriteData), .en(En2), .clk(clk), .Q(sp));  // open: clr
  Register #(.width(32)) register_4 (.D(WriteData), .en(En3), .clk(clk), .Q(gp));  // open: clr
  Register #(.width(32)) register_5 (.D(WriteData), .en(En4), .clk(clk), .Q(tp));  // open: clr
  Register #(.width(32)) register_6 (.D(WriteData), .en(En5), .clk(clk), .Q(t0));  // open: clr
  Register #(.width(32)) register_7 (.D(WriteData), .en(En6), .clk(clk), .Q(t1));  // open: clr
  Register #(.width(32)) register_8 (.D(WriteData), .en(En7), .clk(clk), .Q(t2));  // open: clr
  Register #(.width(32)) register_9 (.D(WriteData), .en(En8), .clk(clk), .Q(s0));  // open: clr
  Register #(.width(32)) register_10 (.D(WriteData), .en(En9), .clk(clk), .Q(s1));  // open: clr
  Register #(.width(32)) register_11 (.D(WriteData), .en(En10), .clk(clk), .Q(a0));  // open: clr
  Register #(.width(32)) register_12 (.D(WriteData), .en(En11), .clk(clk), .Q(a1));  // open: clr
  Register #(.width(32)) register_13 (.D(WriteData), .en(En12), .clk(clk), .Q(a2));  // open: clr
  Register #(.width(32)) register_14 (.D(WriteData), .en(En13), .clk(clk), .Q(a3));  // open: clr
  Register #(.width(32)) register_15 (.D(WriteData), .en(En14), .clk(clk), .Q(a4));  // open: clr
  Register #(.width(32)) register_16 (.D(WriteData), .en(En15), .clk(clk), .Q(a5));  // open: clr
  Register #(.width(32)) register_17 (.D(WriteData), .en(En16), .clk(clk), .Q(a6));  // open: clr
  Register #(.width(32)) register_18 (.D(WriteData), .en(En17), .clk(clk), .Q(a7));  // open: clr
  Register #(.width(32)) register_19 (.D(WriteData), .en(En18), .clk(clk), .Q(s2));  // open: clr
  Register #(.width(32)) register_20 (.D(WriteData), .en(En19), .clk(clk), .Q(s3));  // open: clr
  Register #(.width(32)) register_21 (.D(WriteData), .en(En20), .clk(clk), .Q(s4));  // open: clr
  Register #(.width(32)) register_22 (.D(WriteData), .en(En21), .clk(clk), .Q(s5));  // open: clr
  Register #(.width(32)) register_23 (.D(WriteData), .en(En22), .clk(clk), .Q(s6));  // open: clr
  Register #(.width(32)) register_24 (.D(WriteData), .en(En23), .clk(clk), .Q(s7));  // open: clr
  Register #(.width(32)) register_25 (.D(WriteData), .en(En24), .clk(clk), .Q(s8));  // open: clr
  Register #(.width(32)) register_26 (.D(WriteData), .en(En25), .clk(clk), .Q(s9));  // open: clr
  Register #(.width(32)) register_27 (.D(WriteData), .en(En26), .clk(clk), .Q(s10));  // open: clr
  Register #(.width(32)) register_28 (.D(WriteData), .en(En27), .clk(clk), .Q(s11));  // open: clr
  Register #(.width(32)) register_29 (.D(WriteData), .en(En28), .clk(clk), .Q(t3));  // open: clr
  Register #(.width(32)) register_30 (.D(WriteData), .en(En29), .clk(clk), .Q(t4));  // open: clr
  Register #(.width(32)) register_31 (.D(WriteData), .en(En30), .clk(clk), .Q(t5));  // open: clr
  Register #(.width(32)) register_32 (.D(WriteData), .en(En31), .clk(clk), .Q(t6));  // open: clr
  Multiplexer #(.select(5), .width(32)) multiplexer_1 (
    .in0(zero), .in1(ra), .in2(sp), .in3(gp), .in4(tp), .in5(t0), .in6(t1), .in7(t2), .in8(s0), .in9(s1),
    .in10(a0), .in11(a1), .in12(a2), .in13(a3), .in14(a4), .in15(a5), .in16(a6), .in17(a7), .in18(s2),
    .in19(s3), .in20(s4), .in21(s5), .in22(s6), .in23(s7), .in24(s8), .in25(s9), .in26(s10), .in27(s11),
    .in28(t3), .in29(t4), .in30(t5), .in31(t6), .out(ReadData1), .sel(ReadIndex1));
  Multiplexer #(.select(5), .width(32)) multiplexer_2 (
    .in0(zero), .in1(ra), .in2(sp), .in3(gp), .in4(tp), .in5(t0), .in6(t1), .in7(t2), .in8(s0), .in9(s1),
    .in10(a0), .in11(a1), .in12(a2), .in13(a3), .in14(a4), .in15(a5), .in16(a6), .in17(a7), .in18(s2),
    .in19(s3), .in20(s4), .in21(s5), .in22(s6), .in23(s7), .in24(s8), .in25(s9), .in26(s10), .in27(s11),
    .in28(t3), .in29(t4), .in30(t5), .in31(t6), .out(ReadData2), .sel(ReadIndex2));

  // Notes on the sheet:
  //   INPUTS to your circuit
  //   DON'T CHANGE THE LOCATIONS OF THE INPUTS AND OUTPUTS!
  //   These are DEBUG/TEST outputs from your circuit.
  //   OUTPUTS from your circuit
endmodule
